# Fritzing sketch Glove project fritzing (saved by Fritzing 0.9.3b)
breadboards: 3

parts:
  Bluetooth_RF_Transceiver_HC=_06(ONLYSLAVE) = Bluetooth HC-05 Macho
  ARDUINO_Micro = Arduino Micro (Rev3)
  IR_RECEIVER = TSOP312.., 314.. [package=THT]
  OLED_(SCL=SCK) = Grove OLED 128x96
  THUMB = Basic Flex Resistor
  INDEX = Basic Flex Resistor
  SD_Slot = MicroSD Card Module
  R6 = Resistor [tolerance=±5% resistance=10k package="0805 [SMD]"]
  R7 = Resistor [tolerance=±5% resistance=10k package="0603 [SMD]"]
  MPU_6050 = MPU-6050 Board GY-521 [form="♀ (female)" package=THT]
  Pulse_sensor = Gas Sensor Breakout Board

nets:
  N1: Bluetooth_RF_Transceiver_HC=_06(ONLYSLAVE).TXD, ARDUINO_Micro.D0/RX
  N2: Bluetooth_RF_Transceiver_HC=_06(ONLYSLAVE).RXD, ARDUINO_Micro.D1/TX
  VCC: Bluetooth_RF_Transceiver_HC=_06(ONLYSLAVE).VCC, ARDUINO_Micro.3V3, OLED_(SCL=SCK).VCC, SD_Slot.VCC, Pulse_sensor.H1
  GND: Bluetooth_RF_Transceiver_HC=_06(ONLYSLAVE).GND, ARDUINO_Micro.GND, IR_RECEIVER.GND, OLED_(SCL=SCK).GND, THUMB.pin_1, INDEX.pin_1, SD_Slot.GND, MPU_6050.pin2, Pulse_sensor.GND
  N3: ARDUINO_Micro.MOSI, SD_Slot.MOSI
  N4: ARDUINO_Micro.RXLED/SS, SD_Slot.CS
  N5: ARDUINO_Micro.D2/SDA, OLED_(SCL=SCK).SDA, MPU_6050.pin4
  N6: ARDUINO_Micro.D3/SCL, OLED_(SCL=SCK).SCL, MPU_6050.pin3
  N7: ARDUINO_Micro.SCK, SD_Slot.SCK
  N8: ARDUINO_Micro.MISO, SD_Slot.MISO
  N9: ARDUINO_Micro.5V, IR_RECEIVER.Vs, R6.Pin_0, R7.Pin_0, MPU_6050.pin1
  N10: ARDUINO_Micro.A2, Pulse_sensor.A1
  N11: ARDUINO_Micro.A1, INDEX.Pin_2, R6.Pin_1
  N12: ARDUINO_Micro.A0, THUMB.Pin_2, R7.Pin_1

custom parts:
  MPU-6050 Board GY-521: Acelerometro y Giroscopio MPU-6050 Board GY-521
